// Logisim project MIPSProcessor.circ as structural Verilog
module MIPS32 (
);

  // MIPSProgramROM mipsprogramrom_1: pin names not known
  // Incrementer incrementer_1: pin names not known
  // Mips_ALU mips_alu_1: pin names not known
  // RegisterFile registerfile_1: pin names not known
endmodule

module instructionFetch (
  input  Stall,
  output [31:0] inst,
  output [31:0] PCPlus4
);

  wire clock_1_out;
  wire [31:2] register_1_q;

  Register #(.width(32)) register_1 (
    .D(PCPlus4), .en(Stall), .clk(clock_1_out), .Q({register_1_q, PCPlus4[1:0]}));  // open: clr
  Clock clock_1 (.out(clock_1_out));
  // Incrementer #(.width(30)) incrementer_1: pin names not known; wires that end beside it: Stall, register_1_q, PCPlus4[31:2]
  // MIPSProgramROM mipsprogramrom_1: pin names not known; wires that end beside it: {register_1_q, PCPlus4[1:0]}, inst
endmodule

module instructionDecode (
  input  [31:0] inst,
  input  [31:0] PCPlus4,
  output [31:0] A,
  output [31:0] B,
  output [4:0] Sa,
  output [31:0] imm,
  output SLTIU,
  output [3:0] ctrl,
  output SLTI,
  output I,
  output SLTU,
  output SLT,
  output skip,
  output LUI,
  output MOVN,
  output MOVZ,
  output [31:0] PCPlus4out
);

  wire decode_1_var;
  wire [4:0] decode_1_saout;

  decode decode_1 (
    .Instruction(inst), .SLTIU(SLTIU), .SLTI(SLTI), .I(I), .ctrl(ctrl), .Var(decode_1_var),
    .SaOut(decode_1_saout), .SLTU(SLTU), .SLT(SLT), .skip(skip), .Imm(imm), .LUI(LUI), .MOVN(MOVN),
    .MOVZ(MOVZ));
  // RegisterFile registerfile_1: pin names not known; wires that end beside it: inst[25:21], inst[20:16], A, B
  Multiplexer #(.width(5), .enable("false")) multiplexer_1 (
    .in0(decode_1_saout), .in1(A[4:0]), .out(Sa), .sel(decode_1_var));

  assign PCPlus4out = PCPlus4;
endmodule

module decode (
  input  [31:0] Instruction,
  output SLTIU,
  output SLTI,
  output I,
  output [3:0] ctrl,
  output Var,
  output [4:0] SaOut,
  output SLTU,
  output SLT,
  output skip,
  output [31:0] Imm,
  output LUI,
  output MOVN,
  output MOVZ
);

  wire and_2_out, and_3_out, itype_1_slti, itype_1_sltiu, jbranchtype_1_skip, loadstoretype_1_skip,
       not_1_out, not_2_out, not_3_out, or_1_out, or_2_out, rtype_1_jumpr, rtype_1_movn, rtype_1_movz,
       rtype_1_slt, rtype_1_sltu;
  wire [3:0] itype_1_ctrl, rtype_1_ctrl;

  Rtype rtype_1 (
    .Sa(Instruction[10:6]), .func(Instruction[5:0]), .Var(Var), .SaOut(SaOut), .ctrl(rtype_1_ctrl),
    .SLT(rtype_1_slt), .JumpR(rtype_1_jumpr), .MOVN(rtype_1_movn), .MOVZ(rtype_1_movz), .SLTU(rtype_1_sltu));
  LoadStoreType loadstoretype_1 (.Bit31(Instruction[31]), .skip(loadstoretype_1_skip));
  Itype itype_1 (
    .imm0To15(Instruction[15:0]), .Opcode26To28(Instruction[28:26]), .SLTIU(itype_1_sltiu),
    .SLTI(itype_1_slti), .ctrl(itype_1_ctrl), .Imm(Imm), .LUI(LUI));
  JBranchType jbranchtype_1 (.Bit29(Instruction[29]), .skip(jbranchtype_1_skip));
  or or_1 (or_1_out, loadstoretype_1_skip, jbranchtype_1_skip);
  Multiplexer #(.width(4), .enable("false")) multiplexer_1 (
    .in0(rtype_1_ctrl), .in1(itype_1_ctrl), .out(ctrl), .sel(or_2_out));
  or or_2 (or_2_out, Instruction[26], Instruction[27], Instruction[28], Instruction[29], Instruction[30], Instruction[31]);
  not not_1 (not_1_out, or_2_out);
  and and_1 (I, or_2_out, not_3_out);
  not not_2 (not_2_out, or_2_out);
  and and_2 (and_2_out, or_2_out, or_1_out);
  and and_3 (and_3_out, not_1_out, rtype_1_jumpr);
  and and_4 (SLTIU, itype_1_sltiu, I);
  and and_5 (SLTI, I, itype_1_slti);
  and and_6 (SLTU, rtype_1_sltu, not_2_out);
  and and_7 (SLT, not_2_out, rtype_1_slt);
  not not_3 (not_3_out, skip);
  or or_3 (skip, and_2_out, and_3_out);
  and and_8 (MOVN, not_1_out, rtype_1_movn);
  and and_9 (MOVZ, not_1_out, rtype_1_movz);
endmodule

module Rtype (
  input  [4:0] Sa,
  input  [5:0] func,
  output Var,
  output [4:0] SaOut,
  output [3:0] ctrl,
  output SLT,
  output JumpR,
  output MOVN,
  output MOVZ,
  output SLTU
);

  wire and_3_out, and_5_out, not_1_out, not_2_out, not_3_out, not_4_out, or_1_out, rtype1ops_1_slt,
       rtype1ops_1_sltu, shift_1_var;
  wire [3:0] rtype1ops_1_ctrl, shift_1_ctrl;

  shift shift_1 (.func0to3(func[3:0]), .Sa(Sa), .Var(shift_1_var), .ctrl(shift_1_ctrl), .Saout(SaOut));
  Rtype1Ops rtype1ops_1 (.func0to3(func[3:0]), .SLTU(rtype1ops_1_sltu), .SLT(rtype1ops_1_slt), .ctrl(rtype1ops_1_ctrl));
  not not_1 (not_1_out, func[5]);
  Multiplexer #(.width(4), .enable("false")) multiplexer_1 (
    .in0(shift_1_ctrl), .in1(rtype1ops_1_ctrl), .out(ctrl), .sel(func[5]));
  not not_2 (not_2_out, func[1]);
  and and_1 (SLTU, func[5], rtype1ops_1_sltu);
  and and_2 (SLT, rtype1ops_1_slt, func[5]);
  not not_3 (not_3_out, func[0]);
  or or_1 (or_1_out, SLTU, SLT);
  not not_4 (not_4_out, or_1_out);
  and and_3 (and_3_out, not_4_out, func[3]);
  and and_4 (Var, not_1_out, shift_1_var);
  and and_5 (and_5_out, and_3_out, func[1]);
  and and_6 (JumpR, and_3_out, not_2_out);
  and and_7 (MOVN, func[0], and_5_out);
  and and_8 (MOVZ, and_5_out, not_3_out);
endmodule

module Itype (
  input  [15:0] imm0To15,
  input  [2:0] Opcode26To28,
  output SLTIU,
  output SLTI,
  output [3:0] ctrl,
  output [31:0] Imm,
  output LUI
);

  wire and_1_out, not_1_out, not_2_out, signextended_1_slt, zeroextended_1_lui;
  wire [3:0] signextended_1_ctrl, zeroextended_1_ctrl;
  wire [31:0] signextended_1_immsigned, zeroextended_1_immzero;

  SignExtended signextended_1 (
    .OpCode26To28(Opcode26To28), .imm0To15(imm0To15), .SLT(signextended_1_slt), .ctrl(signextended_1_ctrl),
    .immSigned(signextended_1_immsigned));
  ZeroExtended zeroextended_1 (
    .OpCode26To28(Opcode26To28), .imm0To15(imm0To15), .LUI(zeroextended_1_lui), .ctrl(zeroextended_1_ctrl),
    .immZero(zeroextended_1_immzero));
  not not_1 (not_1_out, Opcode26To28[2]);
  Multiplexer #(.width(4), .enable("false")) multiplexer_1 (
    .in0(signextended_1_ctrl), .in1(zeroextended_1_ctrl), .out(ctrl), .sel(Opcode26To28[2]));
  and and_1 (and_1_out, signextended_1_slt, not_1_out);
  and and_2 (LUI, Opcode26To28[2], zeroextended_1_lui);
  not not_2 (not_2_out, Opcode26To28[0]);
  Multiplexer #(.width(32), .enable("false")) multiplexer_2 (
    .in0(signextended_1_immsigned), .in1(zeroextended_1_immzero), .out(Imm), .sel(Opcode26To28[2]));
  and and_3 (SLTIU, Opcode26To28[0], and_1_out);
  and and_4 (SLTI, not_2_out, and_1_out);
endmodule

module shift (
  input  [3:0] func0to3,
  input  [4:0] Sa,
  output Var,
  output [3:0] ctrl,
  output [4:0] Saout
);

  wire [3:0] shiftsa_1_ctrl, shiftvariable_1_ctrl;

  shiftSa shiftsa_1 (.func0to3(func0to3), .Sa(Sa), .ctrl(shiftsa_1_ctrl), .Saout(Saout));
  shiftVariable shiftvariable_1 (.funct0to3(func0to3), .ctrl(shiftvariable_1_ctrl));
  Multiplexer #(.width(4), .enable("false")) multiplexer_1 (
    .in0(shiftsa_1_ctrl), .in1(shiftvariable_1_ctrl), .out(ctrl), .sel(func0to3[2]));

  assign Var = func0to3[2];
endmodule

module shiftVariable (
  input  [3:0] funct0to3,
  output [3:0] ctrl
);


  assign ctrl = {funct0to3[3], funct0to3[1], funct0to3[3], funct0to3[0]};
endmodule

module shiftSa (
  input  [3:0] func0to3,
  input  [4:0] Sa,
  output [3:0] ctrl,
  output [4:0] Saout
);


  assign ctrl = {func0to3[3], func0to3[1], func0to3[2], func0to3[0]};
  assign Saout = Sa;
endmodule

module Rtype1Ops (
  input  [3:0] func0to3,
  output SLTU,
  output SLT,
  output [3:0] ctrl
);

  wire not_1_out;

  and and_1 (SLTU, func0to3[0], func0to3[3]);
  not not_1 (not_1_out, func0to3[0]);
  and and_2 (SLT, not_1_out, func0to3[3]);

  assign ctrl = {func0to3[2:0], func0to3[3]};
endmodule

module SignExtended (
  input  [2:0] OpCode26To28,
  input  [15:0] imm0To15,
  output SLT,
  output [3:0] ctrl,
  output [31:0] immSigned
);

  assign immSigned[31:15] = {{16{imm0To15[15]}}, imm0To15[15]};  // Bit_Extender bit_extender_1

  assign ctrl = {OpCode26To28, OpCode26To28[2]};
  assign immSigned[14:0] = imm0To15[14:0];
  assign SLT = OpCode26To28[1];
endmodule

module ZeroExtended (
  input  [2:0] OpCode26To28,
  input  [15:0] imm0To15,
  output LUI,
  output [3:0] ctrl,
  output [31:0] immZero
);

  not not_1 (ctrl[0], OpCode26To28[2]);
  assign immZero[31:16] = {{15{ctrl[0]}}, ctrl[0]};  // Bit_Extender bit_extender_1
  and and_1 (LUI, OpCode26To28[1], OpCode26To28[0]);

  assign ctrl[3:1] = OpCode26To28;
  assign immZero[15:0] = imm0To15;
endmodule

module JBranchType (
  input  Bit29,
  output skip
);

  not not_1 (skip, Bit29);
endmodule

module LoadStoreType (
  input  Bit31,
  output skip
);


  assign skip = Bit31;
endmodule

module instructionExcute (
  input  [31:0] A,
  input  [31:0] B,
  input  [4:0] Sa,
  input  [31:0] imm,
  input  SLTIU,
  input  [3:0] ctrl,
  input  SLTI,
  input  I,
  input  SLTU,
  input  SLT,
  input  skip,
  input  LUI,
  input  MOVN,
  input  MOVZ,
  input  [31:0] PCPlus4,
  output [31:0] Aout,
  output [31:0] D,
  output moveOut,
  output skipOut
);

  wire and_1_out, and_2_out, and_3_out, and_4_out, comparator_1_eq, comparator_1_lt, comparator_2_lt,
       not_1_out, not_2_out, not_3_out, or_1_out, or_2_out, or_3_out, or_4_out;
  wire [0:0] multiplexer_4_out;
  wire [31:0] bit_extender_1_out, mips_alu_1_p5, multiplexer_1_out, multiplexer_2_out, multiplexer_3_out,
       multiplexer_5_out;

  or or_1 (or_1_out, SLTI, SLT);
  not not_1 (not_1_out, I);
  or or_2 (or_2_out, SLTIU, SLTU);
  and and_1 (and_1_out, not_1_out, I);
  or or_3 (or_3_out, MOVN, MOVZ);
  Multiplexer #(.width(32), .enable("false")) multiplexer_1 (.in0(B), .in1(imm), .out(multiplexer_1_out), .sel(I));
  or or_4 (or_4_out, or_2_out, or_1_out);
  assign bit_extender_1_out = {{31{and_1_out}}, and_1_out};  // Bit_Extender bit_extender_1
  and and_2 (and_2_out, I, not_2_out);
  not not_2 (not_2_out, or_3_out);
  Multiplexer #(.width(32), .enable("false")) multiplexer_2 (
    .in0(A), .in1(bit_extender_1_out), .out(multiplexer_2_out), .sel(or_3_out));
  Multiplexer #(.width(32), .enable("false")) multiplexer_3 (
    .in0(B), .in1(imm), .out(multiplexer_3_out), .sel(and_2_out));
  // Mips_ALU mips_alu_1: pin names not known; wires that end beside it: A, multiplexer_1_out, ctrl, Sa, mips_alu_1_p5
  Comparator #(.width(32)) comparator_1 (
    .a(multiplexer_2_out), .b(multiplexer_3_out), .eq(comparator_1_eq), .lt(comparator_1_lt));  // open: gt
  Comparator #(.width(32), .mode("unsigned")) comparator_2 (
    .a(A), .b(multiplexer_3_out), .lt(comparator_2_lt));  // open: gt, eq
  Multiplexer #(.enable("false")) multiplexer_4 (
    .in0(comparator_1_lt), .in1(comparator_2_lt), .out(multiplexer_4_out[0]), .sel(or_4_out));
  not not_3 (not_3_out, comparator_1_eq);
  and and_3 (and_3_out, not_3_out, MOVN);
  and and_4 (and_4_out, MOVZ, comparator_1_eq);
  Multiplexer #(.width(32), .enable("false")) multiplexer_5 (
    .in0(mips_alu_1_p5), .in1({bit_extender_1_out[31:1], multiplexer_4_out[0]}), .out(multiplexer_5_out),
    .sel(or_4_out));
  or or_5 (moveOut, and_3_out, and_4_out);
  Multiplexer #(.width(32), .enable("false")) multiplexer_6 (
    .in0(multiplexer_5_out), .in1({imm[15:0], imm[31:16]}), .out(D), .sel(LUI));

  assign Aout = A;
  assign skipOut = skip;
endmodule
